// Logisim project Lab_3_Circuit.circ as structural Verilog: 1 circuit, main circuit main
module main (
  input  x1,
  input  x2,
  output y1,
  output y2
);

  wire clock_1_out, nand_1_out, nand_2_out, nand_3_out, nand_4_out, nand_5_out, nand_6_out, nand_7_out,
       not_1_out, not_2_out, q1_q, q1_qn, q2_q, q2_qn;

  not not_1 (not_1_out, x1);
  not not_2 (not_2_out, x2);
  nand nand_1 (nand_1_out, not_2_out, q1_qn, q2_qn);
  nand nand_2 (nand_2_out, x2, q1_q);
  Clock #(.highDuration(4), .lowDuration(4)) clock_1 (.out(clock_1_out));
  nand nand_3 (nand_3_out, nand_1_out, not_1_out, nand_2_out);
  nand nand_4 (nand_4_out, not_1_out, q2_qn);
  nand nand_5 (nand_5_out, not_1_out, q2_q);
  nand nand_6 (nand_6_out, q1_qn, x2);
  nand nand_7 (nand_7_out, not_2_out, q1_q);
  T_Flip_Flop q1 (.T(nand_3_out), .clk(clock_1_out), .Q(q1_q), .Qn(q1_qn));  // open: reset, preset
  T_Flip_Flop q2 (.T(nand_4_out), .clk(clock_1_out), .Q(q2_q), .Qn(q2_qn));  // open: reset, preset
  nand nand_8 (y1, nand_5_out, nand_6_out);
  nand nand_9 (y2, nand_7_out, not_1_out);
endmodule
